// Logisim project alu.circ as structural Verilog: 1 circuit, main circuit alu
module alu (
  input  [31:0] A,
  input  [31:0] B,
  input  [3:0] ALUSel,
  output [31:0] ALUResult
);

  wire comparator_1_lt;
  wire [31:0] S00, S01, S02, S03, S04, S05, S06, S07, S08, S09, S10, S11, S12, S13, S14;

  Adder #(.width(32)) adder_1 (.a(A), .b(B), .out(S00));  // open: cin, cout
  Subtractor #(.width(32)) subtractor_1 (.a(A), .b(B), .out(S12));  // open: bin, bout
  Multiplier #(.mode("twosComplement"), .width(32)) multiplier_1 (.a(A), .b(B), .out(S08), .cout(S09));  // open: cin
  Multiplier #(.width(32)) multiplier_2 (.a(A), .b(B), .cout(S11));  // open: out, cin
  Shifter #(.shift("lr"), .width(32)) shifter_1 (.in(A), .\dist (B[4:0]), .out(S05));
  Shifter #(.width(32)) shifter_2 (.in(A), .\dist (B[4:0]), .out(S01));
  Shifter #(.shift("ar"), .width(32)) shifter_3 (.in(A), .\dist (B[4:0]), .out(S13));
  assign S04 = A ^ B;  // XOR_Gate xor_1, 32 bits wide
  assign S06 = A | B;  // OR_Gate or_1, 32 bits wide
  assign S07 = A & B;  // AND_Gate and_1, 32 bits wide
  Multiplexer #(.select(4), .width(32)) multiplexer_1 (
    .in0(S00), .in1(S01), .in2(S02), .in3(S03), .in4(S04), .in5(S05), .in6(S06), .in7(S07), .in8(S08),
    .in9(S09), .in10(S10), .in11(S11), .in12(S12), .in13(S13), .in14(S14), .in15(B), .out(ALUResult),
    .sel(ALUSel));
  Comparator #(.width(32)) comparator_1 (.a(A), .b(B), .lt(comparator_1_lt));  // open: gt, eq
  assign S02 = {{31{1'b0}}, comparator_1_lt};  // Bit_Extender bit_extender_1

  // Other names for the same wires on the sheet: BL5[4:0] = B[4:0]; S15[31:0] = B

  // Notes on the sheet:
  //   INPUTS to your circuit
  //   DON'T CHANGE THE LOCATIONS OF THE INPUTS AND OUTPUTS!
  //   OUTPUT from your circuit
endmodule
