// Logisim project control-logic.circ as structural Verilog: 1 circuit, main circuit control_logic
module control_logic (
  input  [31:0] Instruction,
  input  BrEq,
  input  BrLt,
  output PCSel,
  output RegWEn,
  output [2:0] ImmSel,
  output BrUn,
  output ASel,
  output BSel,
  output [3:0] ALUSel,
  output MemWEn,
  output [1:0] WBSel
);

  wire B_Instr, comparator_3_eq, comparator_4_eq, comparator_5_eq, comparator_6_eq, comparator_8_eq,
       comparator_9_eq, comparator_10_eq, comparator_11_eq, comparator_12_eq, comparator_13_eq, isMul,
       isMulh, isMulhu, isSra, isSub, R_Instr;
  wire [3:0] multiplexer_1_out, multiplexer_2_out, multiplexer_3_out, multiplexer_4_out, multiplexer_5_out;
  wire [15:0] rom_1_data;

  Comparator #(.width(7)) comparator_1 (.a(Instruction[6:0]), .b(7'b0010011), .eq(BSel));  // open: gt, lt
  Comparator #(.width(7)) comparator_2 (.a(Instruction[6:0]), .b(7'b0110011), .eq(R_Instr));  // open: gt, lt
  Comparator #(.width(3)) comparator_3 (.a(Instruction[14:12]), .b(3'b001), .eq(comparator_3_eq));  // open: gt, lt
  Comparator #(.width(7)) comparator_4 (.a(Instruction[31:25]), .b(7'b0000001), .eq(comparator_4_eq));  // open: gt, lt
  Comparator #(.width(3)) comparator_5 (.a(Instruction[14:12]), .b(3'b011), .eq(comparator_5_eq));  // open: gt, lt
  Comparator #(.width(7)) comparator_6 (.a(Instruction[31:25]), .b(7'b0000001), .eq(comparator_6_eq));  // open: gt, lt
  Multiplexer #(.select(3), .width(4)) multiplexer_1 (
    .in0(4'b0000), .in1(4'b0001), .in2(4'b0010), .in3(4'b0011), .in4(4'b0100), .in5(4'b0101), .in6(4'b0110),
    .in7(4'b0111), .out(multiplexer_1_out), .sel(Instruction[14:12]));
  ROM #(.addrWidth(6), .dataWidth(16)) rom_1 (.data(rom_1_data));  // open: addr
  and and_1 (isMulh, comparator_3_eq, R_Instr, comparator_4_eq);
  and and_2 (isMulhu, comparator_5_eq, R_Instr, comparator_6_eq);
  Multiplexer #(.width(4)) multiplexer_2 (.in0(multiplexer_1_out), .in1(4'b1000), .out(multiplexer_2_out), .sel(isMul));
  Multiplexer #(.width(4)) multiplexer_3 (
    .in0(multiplexer_2_out), .in1(4'b1001), .out(multiplexer_3_out), .sel(isMulh));
  Multiplexer #(.width(4)) multiplexer_4 (
    .in0(multiplexer_3_out), .in1(4'b1011), .out(multiplexer_4_out), .sel(isMulhu));
  Comparator #(.width(7)) comparator_7 (.a(Instruction[6:0]), .b(7'b1100011), .eq(B_Instr));  // open: gt, lt
  or or_1 (RegWEn, BSel, R_Instr);
  Comparator #(.width(3)) comparator_8 (.a(Instruction[14:12]), .b(3'b000), .eq(comparator_8_eq));  // open: gt, lt
  Comparator #(.width(7)) comparator_9 (.a(Instruction[31:25]), .b(7'b0100000), .eq(comparator_9_eq));  // open: gt, lt
  Comparator #(.width(3)) comparator_10 (.a(Instruction[14:12]), .b(3'b000), .eq(comparator_10_eq));  // open: gt, lt
  Comparator #(.width(7)) comparator_11 (
    .a(Instruction[31:25]), .b(7'b0000001), .eq(comparator_11_eq));  // open: gt, lt
  Multiplexer #(.width(4)) multiplexer_5 (.in0(multiplexer_4_out), .in1(4'b1100), .out(multiplexer_5_out), .sel(isSub));
  Multiplexer #(.width(4)) multiplexer_6 (.in0(multiplexer_5_out), .in1(4'b1101), .out(ALUSel), .sel(isSra));
  and and_3 (isSub, comparator_8_eq, R_Instr, comparator_9_eq);
  and and_4 (isMul, comparator_10_eq, R_Instr, comparator_11_eq);
  Comparator #(.width(3)) comparator_12 (.a(Instruction[14:12]), .b(3'b101), .eq(comparator_12_eq));  // open: gt, lt
  Comparator #(.width(7)) comparator_13 (
    .a(Instruction[31:25]), .b(7'b0100000), .eq(comparator_13_eq));  // open: gt, lt
  and and_5 (isSra, comparator_12_eq, comparator_13_eq);

  // Other names for the same wires on the sheet: I_Instr = BSel; opcode[6:0] = Instruction[6:0];
  //   funct3[2:0] = Instruction[14:12]; funct7[6:0] = Instruction[31:25]

  // Notes on the sheet:
  //   Decode
  //   INPUTS to your circuit
  //   Connect ROM Input here ->
  //   ROM FOR CONTROL LOGIC
  //   DON'T CHANGE THE LOCATIONS OF THE INPUTS AND OUTPUTS!
  //   This is only if you choose to do the ROM option
  //   CONNECT
  //   WIRE
  //   TO
  //   USE
  //   ROM
  //   OUTPUT from your circuit
  //   Reminder: If using ROM, use combinational logic for PCSel
endmodule
