// Logisim project cpu.circ as structural Verilog: 1 circuit, main circuit cpu
module cpu (
  input  clk,
  input  [31:0] Instruction,
  input  [31:0] MemReadData,
  output [31:0] MemAddress,
  output [31:0] ProgramCounter,
  output [31:0] ra,
  output [31:0] sp,
  output [31:0] t0,
  output [31:0] t1,
  output [31:0] t2,
  output [31:0] s0,
  output [31:0] s1,
  output [31:0] a0,
  output [3:0] MemWriteMask,
  output [31:0] MemWriteData
);

  wire BSel, partial_store_1_p1, partial_store_1_p2, partial_store_1_p4, partial_store_1_p6, RegWEn;
  wire [3:0] ALUSel;
  wire [31:0] adder_1_out, ALU_IN_A, ALU_IN_B, ALU_res, Immediate, ReadData2;

  Register #(.width(32)) PC (.D(adder_1_out), .clk(clk), .Q(ProgramCounter));  // open: en, clr
  Adder #(.width(32)) adder_1 (.a(ProgramCounter), .b(32'h4), .out(adder_1_out));  // open: cin, cout
  regfile regfile_1 (
    .ReadIndex1(Instruction[19:15]), .ReadIndex2(Instruction[24:20]), .WriteIndex(Instruction[11:7]),
    .WriteData(ALU_res), .RegWEn(RegWEn), .clk(clk), .ra(ra), .sp(sp), .t0(t0), .t1(t1), .t2(t2), .s0(s0),
    .s1(s1), .a0(a0), .ReadData1(ALU_IN_A), .ReadData2(ReadData2));
  control_logic control_logic_1 (
    .RegWEn(RegWEn), .BSel(BSel), .ALUSel(ALUSel), .Instruction(Instruction));  // open: PCSel, ImmSel, BrUn, ASel, MemWEn, WBSel, BrEq, BrLt
  Multiplexer #(.width(32)) multiplexer_1 (.in0(ReadData2), .in1(Immediate), .out(ALU_IN_B), .sel(BSel));
  imm_gen imm_gen_1 (.Instruction(Instruction), .Immediate(Immediate));  // open: ImmSel
  alu alu_1 (.ALUResult(ALU_res), .A(ALU_IN_A), .B(ALU_IN_B), .ALUSel(ALUSel));
  // branch_comp branch_comp_1: pin names not known
  // partial_store partial_store_1: pin names not known; wires that end beside it: partial_store_1_p1, partial_store_1_p2, partial_store_1_p2, partial_store_1_p4, partial_store_1_p4, partial_store_1_p6, partial_store_1_p1, partial_store_1_p6
  // partial_load partial_load_1: pin names not known

  // Other names for the same wires on the sheet: WriteIndex[4:0] = Instruction[11:7];
  //   ReadIndex1[4:0] = Instruction[19:15]; ReadIndex2[4:0] = Instruction[24:20]; ReadData1[31:0] = ALU_IN_A

  // Notes on the sheet:
  //   To IMEM
  //   IMEM (do **NOT** move this)
  //   From IMEM
  //   Inputs/Outputs for testing. Do **NOT** move these.
  //   To DMEM
  //   DMEM (do **NOT** move this)
  //   From DMEM
endmodule
