// Logisim project regfile.circ as structural Verilog: 1 circuit, main circuit regfile
module regfile (
  input  [4:0] ReadIndex1,
  input  [4:0] ReadIndex2,
  input  [4:0] WriteIndex,
  input  [31:0] WriteData,
  input  RegWEn,
  input  clk,
  output [31:0] ra,
  output [31:0] sp,
  output [31:0] t0,
  output [31:0] t1,
  output [31:0] t2,
  output [31:0] s0,
  output [31:0] s1,
  output [31:0] a0,
  output [31:0] ReadData1,
  output [31:0] ReadData2
);

  wire e0, e1, e2, e3, e4, e5, e6, e7, e8, e9, e10, e11, e12, e13, e14, e15, e16, e17, e18, e19, e20, e21,
       e22, e23, e24, e25, e26, e27, e28, e29, e30, e31;
  wire [31:0] x0, x3, x4, x11, x12, x13, x14, x15, x16, x17, x18, x19, x20, x21, x22, x23, x24, x25, x26,
       x27, x28, x29, x30, x31;

  Multiplexer #(.select(5), .width(32)) multiplexer_1 (
    .in0(x0), .in1(ra), .in2(sp), .in3(x3), .in4(x4), .in5(t0), .in6(t1), .in7(t2), .in8(s0), .in9(s1),
    .in10(a0), .in11(x11), .in12(x12), .in13(x13), .in14(x14), .in15(x15), .in16(x16), .in17(x17),
    .in18(x18), .in19(x19), .in20(x20), .in21(x21), .in22(x22), .in23(x23), .in24(x24), .in25(x25),
    .in26(x26), .in27(x27), .in28(x28), .in29(x29), .in30(x30), .in31(x31), .out(ReadData1), .sel(ReadIndex1));
  Multiplexer #(.select(5), .width(32)) multiplexer_2 (
    .in0(x0), .in1(ra), .in2(sp), .in3(x3), .in4(x4), .in5(t0), .in6(t1), .in7(t2), .in8(s0), .in9(s1),
    .in10(a0), .in11(x11), .in12(x12), .in13(x13), .in14(x14), .in15(x15), .in16(x16), .in17(x17),
    .in18(x18), .in19(x19), .in20(x20), .in21(x21), .in22(x22), .in23(x23), .in24(x24), .in25(x25),
    .in26(x26), .in27(x27), .in28(x28), .in29(x29), .in30(x30), .in31(x31), .out(ReadData2), .sel(ReadIndex2));
  Demultiplexer #(.select(5)) demultiplexer_1 (
    .out0(e0), .out1(e1), .out2(e2), .out3(e3), .out4(e4), .out5(e5), .out6(e6), .out7(e7), .out8(e8),
    .out9(e9), .out10(e10), .out11(e11), .out12(e12), .out13(e13), .out14(e14), .out15(e15), .out16(e16),
    .out17(e17), .out18(e18), .out19(e19), .out20(e20), .out21(e21), .out22(e22), .out23(e23), .out24(e24),
    .out25(e25), .out26(e26), .out27(e27), .out28(e28), .out29(e29), .out30(e30), .out31(e31), .in(RegWEn),
    .sel(WriteIndex));
  Register #(.width(32)) register_1 (.D({32{1'b0}}), .en(e0), .clk(clk), .Q(x0));  // open: clr
  Register #(.width(32)) register_2 (.D(WriteData), .en(e4), .clk(clk), .Q(x4));  // open: clr
  Register #(.width(32)) register_3 (.D(WriteData), .en(e8), .clk(clk), .Q(s0));  // open: clr
  Register #(.width(32)) register_4 (.D(WriteData), .en(e12), .clk(clk), .Q(x12));  // open: clr
  Register #(.width(32)) register_5 (.D(WriteData), .en(e16), .clk(clk), .Q(x16));  // open: clr
  Register #(.width(32)) register_6 (.D(WriteData), .en(e20), .clk(clk), .Q(x20));  // open: clr
  Register #(.width(32)) register_7 (.D(WriteData), .en(e24), .clk(clk), .Q(x24));  // open: clr
  Register #(.width(32)) register_8 (.D(WriteData), .en(e28), .clk(clk), .Q(x28));  // open: clr
  Register #(.width(32)) register_9 (.D(WriteData), .en(e1), .clk(clk), .Q(ra));  // open: clr
  Register #(.width(32)) register_10 (.D(WriteData), .en(e5), .clk(clk), .Q(t0));  // open: clr
  Register #(.width(32)) register_11 (.D(WriteData), .en(e9), .clk(clk), .Q(s1));  // open: clr
  Register #(.width(32)) register_12 (.D(WriteData), .en(e13), .clk(clk), .Q(x13));  // open: clr
  Register #(.width(32)) register_13 (.D(WriteData), .en(e17), .clk(clk), .Q(x17));  // open: clr
  Register #(.width(32)) register_14 (.D(WriteData), .en(e21), .clk(clk), .Q(x21));  // open: clr
  Register #(.width(32)) register_15 (.D(WriteData), .en(e25), .clk(clk), .Q(x25));  // open: clr
  Register #(.width(32)) register_16 (.D(WriteData), .en(e29), .clk(clk), .Q(x29));  // open: clr
  Register #(.width(32)) register_17 (.D(WriteData), .en(e2), .clk(clk), .Q(sp));  // open: clr
  Register #(.width(32)) register_18 (.D(WriteData), .en(e6), .clk(clk), .Q(t1));  // open: clr
  Register #(.width(32)) register_19 (.D(WriteData), .en(e10), .clk(clk), .Q(a0));  // open: clr
  Register #(.width(32)) register_20 (.D(WriteData), .en(e14), .clk(clk), .Q(x14));  // open: clr
  Register #(.width(32)) register_21 (.D(WriteData), .en(e18), .clk(clk), .Q(x18));  // open: clr
  Register #(.width(32)) register_22 (.D(WriteData), .en(e22), .clk(clk), .Q(x22));  // open: clr
  Register #(.width(32)) register_23 (.D(WriteData), .en(e26), .clk(clk), .Q(x26));  // open: clr
  Register #(.width(32)) register_24 (.D(WriteData), .en(e30), .clk(clk), .Q(x30));  // open: clr
  Register #(.width(32)) register_25 (.D(WriteData), .en(e3), .clk(clk), .Q(x3));  // open: clr
  Register #(.width(32)) register_26 (.D(WriteData), .en(e7), .clk(clk), .Q(t2));  // open: clr
  Register #(.width(32)) register_27 (.D(WriteData), .en(e11), .clk(clk), .Q(x11));  // open: clr
  Register #(.width(32)) register_28 (.D(WriteData), .en(e15), .clk(clk), .Q(x15));  // open: clr
  Register #(.width(32)) register_29 (.D(WriteData), .en(e19), .clk(clk), .Q(x19));  // open: clr
  Register #(.width(32)) register_30 (.D(WriteData), .en(e23), .clk(clk), .Q(x23));  // open: clr
  Register #(.width(32)) register_31 (.D(WriteData), .en(e27), .clk(clk), .Q(x27));  // open: clr
  Register #(.width(32)) register_32 (.D(WriteData), .en(e31), .clk(clk), .Q(x31));  // open: clr

  // Other names for the same wires on the sheet: x1[31:0] = ra; x2[31:0] = sp; x5[31:0] = t0; x6[31:0] = t1;
  //   x7[31:0] = t2; x8[31:0] = s0; x9[31:0] = s1; x10[31:0] = a0

  // Notes on the sheet:
  //   Read Circuit
  //   INPUTS to your circuit
  //   alias mapping
  //   DON'T CHANGE THE LOCATIONS OF THE INPUTS AND OUTPUTS!
  //   These are DEBUG/TEST outputs from your circuit.
  //   Write Choose
  //   Write Circuit
  //   OUTPUTS from your circuit
endmodule
